# Fritzing sketch encoder-tester (saved by Fritzing 0.9.2b)
circuit board: 8.46667cm x 5.64444cm
breadboards: 1

parts:
  Part1 = Arduino Uno (Rev3)
  IdxL = LED - 3mm [color="Red (633nm)" package="3 mm [THT]"]
  5VL = LED - 3mm [color="Green (570nm)" package="3 mm [THT]"]
  ChBL = LED - 3mm [color="Blue (525nm)" package="3 mm [THT]"]
  3V3L = LED - 3mm [color="Blue (525nm)" package="3 mm [THT]"]
  ChAL = LED - 3mm [color="Green (570nm)" package="3 mm [THT]"]
  R1 = Resistor [tolerance=±5% resistance=2.2k package=THT]
  R2 = Resistor [tolerance=±5% resistance=2.2k package=THT]
  R4 = Resistor [tolerance=±5% resistance=620 package=THT]
  J1 = male pin header, 2 pins [form="♂ (male)"]
  ChA = male pin header, 3 pins [form="♂ (male)"]
  ChB = male pin header, 3 pins [form="♂ (male)"]
  Idx = male pin header, 3 pins [form="♂ (male)"]
  R6 = Resistor [tolerance=±5% resistance=10k package=THT]
  BUT = Pushbutton [package="[THT]"]
  SPD = Rotary Potentiometer (Small) [maximum_resistance=100kΩ package=THT]
  PWM = male pin header, 3 pins [form="♂ (male)"]
  PWMF = female pin header, 3 pins [form="♀ (female)"]
  FwdL = LED - 3mm [color="Green (570nm)" package="3 mm [THT]"]
  RevL = LED - 3mm [color="Red (633nm)" package="3 mm [THT]"]
  R7 = Resistor [tolerance=±5% resistance=510 package=THT]
  R8 = Resistor [tolerance=±5% resistance=750 package=THT]
  R9 = Resistor [tolerance=±5% resistance=3.3k package=THT]
  R10 = Resistor [tolerance=±5% resistance=4.7k package=THT]
  AIN = female pin header, 3 pins [form="♀ (female)"]
  AINM = male pin header, 3 pins [form="♂ (male)"]
  LEDTST = female pin header, 5 pins [form="♀ (female)"]
  Encoder = female pin header, 5 pins [form="♀ (female)"]
  REV = female pin header, 3 pins [form="♀ (female)"]
  RELAY = female pin header, 3 pins [form="♀ (female)"]
  FWD = female pin header, 3 pins [form="♀ (female)"]
  5V = female pin header, 2 pins [form="♀ (female)"]
  3V3 = female pin header, 2 pins [form="♀ (female)"]

nets:
  N1: Part1.A0, SPD.wiper
  N2: Part1.A1, AIN.pin3, AINM.pin3
  N3: Part1.D8, ChAL.anode
  N4: Part1.D10_PWM/SS, ChBL.anode
  N5: Part1.D11_PWM/MOSI, FwdL.anode, RELAY.pin3, FWD.pin3
  N6: Part1.D12/MISO, IdxL.anode
  N7: Part1.D13/SCK, RevL.anode, REV.pin3, RELAY.pin2
  N8: Part1.GND, R1.Pin_1, R2.Pin_0, R4.Pin_1, ChA.pin1, ChB.pin1, Idx.pin1, BUT.Pin_1, BUT.Pin_2, SPD.leg1, PWM.pin1, PWMF.pin1, R7.Pin_1, R8.Pin_1, R9.Pin_0, R10.Pin_0, AIN.pin1, AINM.pin1, LEDTST.pin5, Encoder.pin1, REV.pin1, RELAY.pin1, FWD.pin1, 5V.pin1, 3V3.pin2
  N9: Part1.D2, ChA.pin3, Encoder.pin3
  N10: Part1.D3_PWM, ChB.pin3, Encoder.pin5
  N11: Part1.D4, Idx.pin3, Encoder.pin2
  N12: Part1.D5_PWM, PWM.pin3, PWMF.pin3
  N13: Part1.D7, R6.Pin_0, BUT.Pin_3, BUT.Pin_4
  N14: Part1.3V3, 3V3L.anode, LEDTST.pin2, 3V3.pin1
  N15: Part1.5V, 5VL.anode, J1.pin1, R6.Pin_1, SPD.leg2, AIN.pin2, AINM.pin2, LEDTST.pin1, REV.pin2, FWD.pin2, 5V.pin2
  N16: IdxL.cathode, R8.Pin_0
  N17: 5VL.cathode, R1.Pin_0
  N18: ChBL.cathode, R7.Pin_0
  N19: 3V3L.cathode, R2.Pin_1
  N20: ChAL.cathode, R4.Pin_0
  N21: J1.pin2, ChA.pin2, ChB.pin2, Idx.pin2, Encoder.pin4
  N22: PWM.pin2, PWMF.pin2
  N23: FwdL.cathode, R9.Pin_1
  N24: RevL.cathode, R10.Pin_1
  N25: LEDTST.pin3, LEDTST.pin4

notes:
  ChA, ChB, Idx broken out two 3 PWM male headers (identical to roboRIO inputs)
  3 LEDs to indicate state. ChA - green, ChB - blue, Idx - red.
  Two pin header that you can jumper if you want to provide 5V on the middle (red) line of the PWM ports.
  Button A
  * Quick press dumps report, bumps relay state, and toggles PWM control
  * Hold for 0.5 secs to zero
  Blue LED for 3V3 power bus indicator and Green LED for 5V power bus. Four pin female header if you want to plug in for power.
  Resistor values on LEDs are not critical. I tried to keep the ChA, ChB, and Idx indicators around 3 ma and the power indicators below 1 ma
  Support PWM speed control, however only allow user to adjust speed while report button is pressed (analog reads are slow)
  TODO/Fix:
  * Add 2nd PWM output (PIN 6)
  * Add 2nd Spd Control
  * Use PIN 9 instead of PIN 13 for Rev
  * Should PWM be on 9, 10?

// code stored in the sketch: EncoderTest.ino
/*
 *
 * Encoder test program.
 * 
 * Plug ChA from encoder into PIN 2
 * Plug ChB from encoder into PIN 3
 * Plug Idx from encoder into PIN 4 (Optional)
 * Plug GND and 5V from Encoder into Arduino
 * 
 * Optional
 * 
 * LED on PIN 8 will show state of ChA (Green LED)
 * LED on PIN 10 will show state of ChB (Blue LED)
 * LED on PIN 12 will show state of Idx (Red LED)
 * 
 */

// constants won't change. They're used here to
// set pin numbers:

// LED output pins for each channel of encoder
const int ledA = 8;
const int ledB = 10;
const int ledI = 12;

// Input PINS for data from encoder
const int CHA_PIN = 2;
const int CHB_PIN = 3;
const int IDX_PIN = 4;
const int REPORT_PIN = 7;

const int MOTOR0_PIN = 5;
const int SPEED0_PIN = 0;

// Relay (and two digital outputs)
const int FWD_PIN = 11;
const int REV_PIN = 13;

String padLeading(String sval, int places) {
  int slen = sval.length();
  
  const int maxPlaces = 20;
  places = min(places, maxPlaces);
  
  if (slen < places) {
    // 20 space characters
    const char* spaces = "                    ";
    String pad(&spaces[maxPlaces - (places - slen)]);
    sval = pad + sval;
  }
  return sval;
}
  
String formatFixed(unsigned long val, int places) {
  String valStr(val);
  return padLeading(valStr, places);
}
